# Fritzing sketch pressure (saved by Fritzing 0.9.3b)
breadboards: 1

parts:
  パーツ1 = Arduino Nano (Rev3.0)
  J1 = Basic Force Sensing Resistor (FSR) [package=THT]
  R1 = Resistor [tolerance=±5% resistance=100 package=THT]

nets:
  N1: パーツ1.GND, J1.pin_1
  N2: パーツ1.5V, R1.Pin_0
  N3: パーツ1.A0, J1.pin_0, R1.Pin_1
